// Logisim project ppu.circ as structural Verilog: 1 circuit, main circuit main
module main (
);

  wire and_1_out, and_2_out, clock_1_out, clock_2_out, comparator_1_eq, comparator_2_eq, comparator_3_eq,
       comparator_4_eq, comparator_5_eq, comparator_6_eq, counter_1_carry, counter_2_carry;
  wire [3:0] counter_1_q, counter_2_q, counter_4_q;
  wire [11:0] counter_3_q;

  Counter #(.max('hf), .width(4)) counter_1 (
    .clr(and_2_out), .count(clock_1_out), .clk(clock_1_out), .carry(counter_1_carry), .Q(counter_1_q));  // open: load, up, D
  Clock clock_1 (.out(clock_1_out));
  Counter #(.max('hf), .width(4)) counter_2 (
    .clr(and_2_out), .count(counter_1_carry), .clk(counter_1_carry), .carry(counter_2_carry), .Q(counter_2_q));  // open: load, up, D
  Comparator #(.width(4)) comparator_1 (.a(4'b1111), .b(counter_1_q), .eq(comparator_1_eq));  // open: gt, lt
  Counter #(.max('hfff), .width(12)) counter_3 (
    .clr(comparator_3_eq), .count(clock_2_out), .clk(clock_2_out), .Q(counter_3_q));  // open: load, up, D, carry
  Clock clock_2 (.out(clock_2_out));
  and and_1 (and_1_out, comparator_1_eq, comparator_2_eq);
  Counter #(.max('hf), .width(4)) counter_4 (
    .clr(and_2_out), .count(counter_2_carry), .clk(counter_2_carry), .Q(counter_4_q));  // open: load, up, D, carry
  and and_2 (and_2_out, and_1_out, comparator_6_eq);
  Comparator #(.width(4)) comparator_2 (.a(4'b0001), .b(counter_2_q), .eq(comparator_2_eq));  // open: gt, lt
  Comparator #(.width(12)) comparator_3 (.a(12'h2fa), .b(counter_3_q), .eq(comparator_3_eq));  // open: gt, lt
  Comparator #(.width(12)) comparator_4 (.a({12{1'b0}}), .b(counter_3_q), .eq(comparator_4_eq));  // open: gt, lt
  Comparator #(.width(12)) comparator_5 (.a(12'h5b), .b(counter_3_q), .eq(comparator_5_eq));  // open: gt, lt
  Comparator #(.width(4)) comparator_6 (.a(4'b0011), .b(counter_4_q), .eq(comparator_6_eq));  // open: gt, lt
  D_Flip_Flop d_ff_1 (.clk(comparator_4_eq), .preset(comparator_5_eq));  // open: D, Q, Qn, reset
endmodule
